// Logisim project lab-7_q.circ as structural Verilog
module main (
  input  [3:0] in_1,
  input  [3:0] in_2,
  input  in_3,
  input  in_4
);

  wire clk_2phase_1_phi_1, clk_2phase_1_phi_2, comparator_1_lt;
  wire [3:0] adder_1_out, multiplexer_1_out, register_1_q, register_2_q;

  Register #(.width(4)) register_1 (.D(register_2_q), .Q(register_1_q), .clk(clk_2phase_1_phi_1));  // open: en, clr
  Adder #(.width(4)) adder_1 (.a(4'b0001), .b(register_1_q), .out(adder_1_out));  // open: cin, cout
  Comparator #(.width(4)) comparator_1 (.a(adder_1_out), .b(in_1), .lt(comparator_1_lt));  // open: gt, eq
  clk_2phase clk_2phase_1 (.phi_1(clk_2phase_1_phi_1), .phi_2(clk_2phase_1_phi_2));
  Multiplexer #(.select(2), .width(4), .enable("false")) multiplexer_1 (
    .in1(in_2), .in2(adder_1_out), .in3(register_1_q), .out(multiplexer_1_out), .sel({in_4, in_3}));  // open: in0
  Register #(.width(4)) register_2 (
    .D(multiplexer_1_out), .Q(register_2_q), .clk(clk_2phase_1_phi_2));  // open: en, clr

  // Notes on the sheet:
  //   i
  //   cmp
endmodule

// CLK
module clk_2phase (
  output phi_1,
  output phi_2
);

  wire clock_1_out, nand_1_out, nand_2_out, not_1_out, not_2_out, not_3_out;

  Clock clock_1 (.out(clock_1_out));
  not not_1 (not_1_out, clock_1_out);
  nand nand_1 (nand_1_out, not_1_out, phi_2);
  not not_2 (not_2_out, nand_1_out);
  nand nand_2 (nand_2_out, phi_1, clock_1_out);
  not not_3 (not_3_out, nand_2_out);
  not not_4 (phi_1, not_2_out);
  not not_5 (phi_2, not_3_out);
endmodule
