// Logisim project traffic_light_fsm.circ as structural Verilog: 2 circuits, main circuit clk_2phase
module main (
  input  rst
);

  wire and_1_out, and_2_out, and_3_out, and_4_out, and_5_out, and_6_out, and_7_out, and_8_out, and_9_out,
       and_10_out, and_11_out, and_12_out, and_13_out, and_14_out, and_15_out, clk_2phase_1_phi_1,
       clk_2phase_1_phi_2, not_1_out, not_2_out, not_3_out, not_4_out, not_5_out, not_6_out, not_7_out,
       not_8_out, not_9_out, not_10_out, not_11_out, not_12_out, not_13_out, not_14_out, not_15_out,
       not_16_out, not_17_out, not_18_out, not_19_out, not_20_out, not_21_out, not_22_out, not_23_out,
       not_24_out, or_1_out, or_2_out, or_3_out, or_4_out, or_5_out, or_6_out, Q0_q, Q1_q, Q2_q, Q_prime_0_q,
       Q_prime_1_q, Q_prime_2_q;

  clk_2phase clk_2phase_1 (.phi_1(clk_2phase_1_phi_1), .phi_2(clk_2phase_1_phi_2));
  D_Flip_Flop #(.trigger("high")) Q_prime_2 (
    .clk(clk_2phase_1_phi_1), .D(or_1_out), .Q(Q_prime_2_q));  // open: Qn, preset, en, reset
  D_Flip_Flop #(.trigger("high")) Q2 (
    .clk(clk_2phase_1_phi_2), .D(Q_prime_2_q), .Q(Q2_q));  // open: Qn, preset, en, reset
  D_Flip_Flop #(.trigger("high")) Q_prime_1 (
    .clk(clk_2phase_1_phi_1), .D(or_2_out), .Q(Q_prime_1_q));  // open: Qn, preset, en, reset
  D_Flip_Flop #(.trigger("high")) Q1 (
    .clk(clk_2phase_1_phi_2), .D(Q_prime_1_q), .Q(Q1_q));  // open: Qn, preset, en, reset
  D_Flip_Flop #(.trigger("high")) Q_prime_0 (
    .clk(clk_2phase_1_phi_1), .D(or_3_out), .Q(Q_prime_0_q));  // open: Qn, preset, en, reset
  D_Flip_Flop #(.trigger("high")) Q0 (
    .clk(clk_2phase_1_phi_2), .D(Q_prime_0_q), .Q(Q0_q));  // open: Qn, preset, en, reset
  not not_1 (not_1_out, Q1_q);
  not not_2 (not_2_out, Q0_q);
  not not_3 (not_3_out, Q2_q);
  not not_4 (not_4_out, Q0_q);
  not not_5 (not_5_out, Q2_q);
  not not_6 (not_6_out, Q1_q);
  not not_7 (not_7_out, Q2_q);
  not not_8 (not_8_out, Q0_q);
  not not_9 (not_9_out, rst);
  not not_10 (not_10_out, Q0_q);
  not not_11 (not_11_out, Q1_q);
  not not_12 (not_12_out, rst);
  and and_1 (and_1_out, Q0_q, Q1_q);
  and and_2 (and_2_out, Q2_q, not_1_out, not_2_out);
  and and_3 (and_3_out, not_3_out, Q1_q, not_4_out);
  and and_4 (and_4_out, not_5_out, not_6_out, Q0_q);
  and and_5 (and_5_out, not_7_out, not_8_out, not_9_out);
  and and_6 (and_6_out, not_10_out, not_11_out, not_12_out);
  or or_1 (or_1_out, and_1_out, and_2_out, rst);
  or or_2 (or_2_out, and_3_out, and_4_out, rst);
  or or_3 (or_3_out, and_5_out, and_6_out);
  LED led_1 (.in(and_8_out));
  LED led_2 (.in(and_7_out));
  LED led_3 (.in(or_4_out));
  not not_13 (not_13_out, Q0_q);
  LED led_4 (.in(and_15_out));
  LED led_5 (.in(or_6_out));
  LED led_6 (.in(or_5_out));
  and and_7 (and_7_out, Q0_q, not_16_out);
  and and_8 (and_8_out, not_13_out, not_15_out, not_14_out);
  not not_14 (not_14_out, Q2_q);
  not not_15 (not_15_out, Q1_q);
  or or_4 (or_4_out, Q1_q, and_9_out);
  and and_9 (and_9_out, not_17_out, Q2_q);
  not not_16 (not_16_out, Q1_q);
  not not_17 (not_17_out, Q0_q);
  and and_10 (and_10_out, not_18_out, not_19_out);
  not not_18 (not_18_out, Q2_q);
  not not_19 (not_19_out, Q1_q);
  or or_5 (or_5_out, and_10_out, and_11_out, and_12_out);
  and and_11 (and_11_out, not_20_out, Q0_q);
  not not_20 (not_20_out, Q1_q);
  and and_12 (and_12_out, Q1_q, Q2_q);
  and and_13 (and_13_out, not_21_out, Q1_q, not_22_out);
  not not_21 (not_21_out, Q0_q);
  or or_6 (or_6_out, and_13_out, and_14_out);
  and and_14 (and_14_out, not_23_out, not_24_out, Q2_q);
  not not_22 (not_22_out, Q2_q);
  not not_23 (not_23_out, Q0_q);
  not not_24 (not_24_out, Q1_q);
  and and_15 (and_15_out, Q0_q, Q1_q);

  // Notes on the sheet:
  //   Current State
  //   Transition State
  //   Q0
  //   Q1
  //   Q2
  //   Main
  //   Connecting Road
endmodule

// CLK
module clk_2phase (
  output phi_1,
  output phi_2
);

  wire clock_1_out, nand_1_out, nand_2_out, not_1_out, not_2_out, not_3_out;

  Clock clock_1 (.out(clock_1_out));
  not not_1 (not_1_out, clock_1_out);
  nand nand_1 (nand_1_out, not_1_out, phi_2);
  not not_2 (not_2_out, nand_1_out);
  not not_3 (not_3_out, nand_2_out);
  nand nand_2 (nand_2_out, phi_1, clock_1_out);
  not not_4 (phi_1, not_2_out);
  not not_5 (phi_2, not_3_out);
endmodule
