// Logisim project week04.circ as structural Verilog: 3 circuits, main circuit main
module main (
  input  in_1,
  input  in_2,
  input  in_3,
  input  in_4,
  input  in_5,
  output out_6,
  output out_7
);

  wire full_adder_1_c0;

  Full_Adder full_adder_1 (.ci(in_5), .x(in_2), .y(in_1), .c0(full_adder_1_c0), .s(out_6));
  Full_Adder full_adder_2 (.ci(full_adder_1_c0), .x(in_4), .y(in_3), .s(out_7));  // open: c0
  Full_Adder full_adder_3 ();  // open: ci, x, y, c0, s
  Full_Adder full_adder_4 ();  // open: ci, x, y, c0, s
endmodule

module _1_Bit_Multiplexer (
  input  in_1,
  input  in_2,
  input  in_3,
  output out_4
);

  wire and_1_out, and_2_out, not_1_out;

  not not_1 (not_1_out, in_3);
  and and_1 (and_1_out, in_1, not_1_out);
  and and_2 (and_2_out, in_2, in_3);
  or or_1 (out_4, and_1_out, and_2_out);
endmodule

module Full_Adder (
  input  ci,
  input  x,
  input  y,
  output s,
  output c0
);

  wire and_1_out, and_2_out, xor_1_out;

  and and_1 (and_1_out, y, x);
  xor xor_1 (xor_1_out, x, y);
  or or_1 (c0, and_1_out, and_2_out);
  and and_2 (and_2_out, xor_1_out, ci);
  xor xor_2 (s, xor_1_out, ci);

  // Notes on the sheet:
  //   x
  //   y
endmodule
